# Fritzing sketch Nodo Master - Progetto (saved by Fritzing 0.9.3b)
breadboards: 1

parts:
  ESP8266_ESP-12E = Gizwits WiFi Witty ESP-12F
  IR1 = TSOP312.., 314.. [package=THT]
  LED1 = LED - 5mm [color="Infrared (940nm)" package="5 mm [THT]"]
  R1 = Resistor [tolerance=±5% resistance=220 package=THT]

nets:
  N1: ESP8266_ESP-12E.GPIO13, R1.Pin_0
  N2: ESP8266_ESP-12E.VCC, IR1.Vs
  GND: ESP8266_ESP-12E.GND, IR1.GND, LED1.cathode
  N3: ESP8266_ESP-12E.GPIO15, IR1.Data
  N4: LED1.anode, R1.Pin_1
