# Fritzing sketch Nodo Master (saved by Fritzing 0.9.3b)
breadboards: 1

parts:
  Gizwits_WiFi_Witty_ESP-12F1 = Gizwits WiFi Witty ESP-12F
  R2 = Resistor [tolerance=±5% resistance=100 package=THT]
  LED3 = LED - 5mm [color="Infrared (940nm)" package="5 mm [THT]"]
  R3 = Resistor [tolerance=±5% resistance=100 package=THT]
  Relè = LED - 5mm [color="Red (633nm)" package="5 mm [THT]"]
  IR1 = TSOP312.., 314.. [package=THT]
  LCD1 = LCD screen

nets:
  N1: Gizwits_WiFi_Witty_ESP-12F1.GPIO14, R3.Pin_1
  VCC: Gizwits_WiFi_Witty_ESP-12F1.VCC, IR1.Data, LCD1.VDD
  GND: Gizwits_WiFi_Witty_ESP-12F1.GND, IR1.Vs, LCD1.VSS
  N2: Gizwits_WiFi_Witty_ESP-12F1.GPIO15, R2.Pin_1
  N3: Gizwits_WiFi_Witty_ESP-12F1.GPIO2, IR1.GND
  N4: Gizwits_WiFi_Witty_ESP-12F1.GPIO4, LCD1.V0
  N5: Gizwits_WiFi_Witty_ESP-12F1.GPIO5, LCD1.RS
  N6: R2.Pin_0, Relè.anode
  N7: LED3.anode, R3.Pin_0

notes:
  Display LCD 16 segmenti X 2 con modulo I2C
